# Fritzing sketch ouivalo_schematic_protoV1 (saved by Fritzing 0.8.7b)
breadboards: 1

parts:
  MKRFox1 = Arduino MKR Fox 1200
  LED1 = smd LED [color="Red (633nm)" package="1206 [SMD]"]
  LED2 = smd LED [color="Yellow (592nm)" package="1206 [SMD]"]
  LED3 = smd LED [color="Blue (430nm)" package="1206 [SMD]"]
  S2 = Pushbutton [package="[THT]"]
  Part2 = RFID-RC522-v2
  J1 = Piezo Speaker
  R1 = Resistor [tolerance=±5% resistance=1k package=THT]
  R2 = Resistor [tolerance=±5% resistance=1k package=THT]
  R3 = Resistor [tolerance=±5% resistance=1k package=THT]
  R4 = Resistor [tolerance=±5% resistance=150 package=THT]
  M1 = DC Motor
  S3 = Pushbutton [package="[THT]"]
  PART1 = Motor Driver 1A Dual TB6612FNG [part_number=ROB_09457]
  S5 = Magnetic Door Switch [package=reed_switch_plastic]
  D2F1 = D2F-FL Omron Snap Action Limit Switch with Level
  D2F2 = D2F-FL Omron Snap Action Limit Switch with Level
  R5 = Resistor [tolerance=±5% resistance=150 package=THT]
  VCC1 = Battery
  U1 = Voltage Regulator -- 3.3 V -- LM1117
  R6 = Resistor [tolerance=±5% resistance=150 package=THT]
  Voltmeter_(DC)1 = Multimeter (DC Voltage)
  R7 = Resistor [tolerance=±5% resistance=220 package="0603 [SMD]"]
  R8 = Resistor [tolerance=±5% resistance=220 package="0603 [SMD]"]
  KY-1 = Keyes Relay [package=THT]
  M2 = BME280

nets:
  GND: MKRFox1.GND, MKRFox1.7, LED1.cathode, LED2.cathode, LED3.cathode, S2.Pin_1, S2.Pin_2, Part2.SDA, Part2.GND, J1.pin1, D2F1.NO, D2F2.NO, R5.Pin_0, VCC1.-, U1.GND, R6.Pin_0, KY-1.ground
  N1: MKRFox1.A1, S5.2
  N2: MKRFox1.A2, PART1.BIN2
  N3: MKRFox1.A3, PART1.BIN1
  N4: MKRFox1.A5, KY-1.signal
  N5: MKRFox1.A6, D2F1.NC
  N6: MKRFox1.0, S2.Pin_3, S2.Pin_4
  N7: MKRFox1.1, S3.Pin_3, S3.Pin_4
  N8: MKRFox1.D2_PWM, R3.Pin_1
  N9: MKRFox1.D3_PWM, R2.Pin_1
  N10: MKRFox1.D4_PWM, R1.Pin_1
  N11: MKRFox1.D5_PWM, R4.Pin_0
  N12: MKRFox1.VCC, U1.IN
  N13: MKRFox1.14/TX, D2F2.NC
  N14: MKRFox1.13/RX, R5.Pin_1
  N15: MKRFox1.12/SCL, M2.SCL
  N16: MKRFox1.11/SDA, M2.SDA
  N17: MKRFox1.10/MISO, Part2.MISO
  N18: MKRFox1.9/SCK, Part2.SCK
  N19: MKRFox1.8/MOSI, Part2.MOSI
  N20: MKRFox1.6, Part2.RST
  N21: LED1.anode, R3.Pin_0
  N22: LED2.anode, R2.Pin_0
  N23: LED3.anode, R1.Pin_0
  N24: Part2.3.3V, KY-1.C
  N25: J1.pin2, R4.Pin_1
  N26: M1.pin_1, PART1.B01
  N27: M1.pin_2, PART1.B02
  N28: S3.Pin_1, S3.Pin_2, PART1.GND, S5.1, KY-1.NO
  N29: PART1.VM, PART1.VCC, VCC1.+
  N30: U1.OUT, Voltmeter_(DC)1.COM_Probe, R7.Pin_1
  N31: R8.Pin_0, R8.Pin_1

notes:
  BIN2
  BIN1
  STBY
  BO1/BO2
  VMM/NC
  SDA
  SCK
  MOSI
  MISO
  RST
  Pour le DEBUG
  ALERTE
  MSG
  HT7333

custom parts:
  RFID-RC522-v2: A simple China made RFID-RC522 Reader; do check the pin labels, as this is a MFRC522 based clone.
  Motor Driver 1A Dual TB6612FNG: The TB6612FNG motor driver can control up to two DC motors at a constant current of 1.2A (3.2A peak). Two input signals (IN1 and IN2) can be used to control the motor in one of four function modes - CW, CCW, short-brake, and stop. The two motor outputs (A and B) can be separately controlled, the speed of each motor is controlled via a PWM input signal with a frequency up to 100kHz. The STBY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
  D2F-FL Omron Snap Action Limit Switch with Level: Snap action switch with stainless steel lever.
  Voltage Regulator -- 3.3 V -- LM1117: LM1117-3.3 Voltage regulator, 3.3 V output. Note that the pinout order is not the same as LM7805 or LM7833.
  Multimeter (DC Voltage): A standard multimeter to measure volatages, currents and resistances
  Keyes Relay: The Keyes 5V relay module is suitable for SCM development, home appliance control. It uses a 5V~12V TIL control signal which can control DC / AC signal.
  BME280: Temperature Humidity Barometric presure Sensor
